# Fritzing sketch fritzing (saved by Fritzing 0.9.4)
breadboards: 1

parts:
  Nokia_5110_LCD_Module1 = Nokia 5110 LCD
  Parça1 = Arduino Uno (Rev3)
  R1 = Resistor [tolerance=±5% resistance=220 package=THT]
  R2 = Resistor [tolerance=±5% resistance=220 package=THT]
  R3 = Resistor [tolerance=±5% resistance=220 package=THT]
  R4 = Resistor [tolerance=±5% resistance=220 package=THT]
  LED1 = LED - 5mm [color="Red (633nm)" package="5 mm [THT]"]
  LED2 = LED - 5mm [color="Red (633nm)" package="5 mm [THT]"]
  S1 = Pushbutton [package="[THT]"]
  S2 = Pushbutton [package="[THT]"]
  J1 = Piezo Speaker
  R5 = Resistor [tolerance=±5% resistance=220 package=THT]

nets:
  N1: Nokia_5110_LCD_Module1.VCC, Parça1.D3_PWM
  N2: Nokia_5110_LCD_Module1.GND, Parça1.D4
  N3: Nokia_5110_LCD_Module1.SCE, Parça1.D5_PWM
  N4: Nokia_5110_LCD_Module1.RST, Parça1.D6_PWM
  N5: Nokia_5110_LCD_Module1.D/C, Parça1.D7
  N6: Nokia_5110_LCD_Module1.DN(MOSI), Nokia_5110_LCD_Module1.SCLK, Parça1.5V
  N7: Nokia_5110_LCD_Module1.LED, Nokia_5110_LCD_Module1.LED_(out), Parça1.GND, R1.Pin_0, R2.Pin_0, LED1.anode, LED2.anode, J1.pin1
  N8: Parça1.D9_PWM, R1.Pin_1, S2.Pin_3, S2.Pin_4
  N9: Parça1.D10_PWM/SS, R3.Pin_0
  N10: Parça1.D11_PWM/MOSI, R4.Pin_0
  N11: Parça1.D12/MISO, R5.Pin_1
  N12: Parça1.D2, R2.Pin_1, S1.Pin_3, S1.Pin_4
  N13: Parça1.3V3, S1.Pin_1, S1.Pin_2, S2.Pin_1, S2.Pin_2
  N14: R3.Pin_1, LED2.cathode
  N15: R4.Pin_1, LED1.cathode
  N16: J1.pin2, R5.Pin_0

custom parts:
  Nokia 5110 LCD: Nokia 5110 Graphic 84*48 LCD module such as the Sparkfun LCD-10168 or the clones from Ebay. There is example code for the Arduino available from the Sparkfun site in https://learn.sparkfun.com/tutorials/graphic-lcd-hookup-guide This is a 3.3V device, if you are running it from a 5V micro you need a 5V tolorant level translator such as the 74ahc367 to protect the signal imputs. Rafa G. did a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
